// Logisim project ALU.circ as structural Verilog: 1 circuit, main circuit main
module main (
  input  A3,
  input  A2,
  input  A1,
  input  A0,
  input  B3,
  input  B2,
  input  B1,
  input  B0,
  input  Cs0,
  input  Cs1,
  input  Cs2,
  output S3,
  output S2,
  output S1,
  output S0,
  output Cout,
  output V,
  output S,
  output C,
  output Z
);

  wire n7404_1_p2, n7404_1_p4, n7404_1_p6, n7404_1_p9, n7404_1_p10, n7404_1_p11, n7404_1_p12, n7404_1_p13,
       n7404_1_p14, n7408_1_p3, n7408_1_p6, n7408_2_p3, n7432_1_p4, n7432_1_p5, n7432_1_p6, n7483_1_p7,
       n7486_1_p3, n7486_1_p6, n7486_1_p11, n7486_1_p14, n7486_2_p3, n7486_2_p6, n7486_2_p11, n7486_2_p14,
       n74157_1_p4, n74157_1_p7, n74157_1_p13, n74157_1_p16, n74157_2_p4, n74157_2_p7, n74157_2_p9,
       n74157_2_p12, n74157_2_p15;

  // _7404 7404_1: pin names not known; wires that end beside it: Cs0, n7404_1_p2, Cs1, n7404_1_p4, Cs2, n7404_1_p6, 1'b0, 1'b1, n7404_1_p9, n7404_1_p10, n7404_1_p11, n7404_1_p12, n7404_1_p13, n7404_1_p14
  // _7486 7486_1: pin names not known; wires that end beside it: A3, B3, n7486_1_p3, A2, B2, n7486_1_p6, 1'b0, 1'b1, B0, A0, n7486_1_p11, B1, A1, n7486_1_p14
  // _7486 7486_2: pin names not known; wires that end beside it: B3, Cs0, n7486_2_p3, B2, Cs0, n7486_2_p6, 1'b0, 1'b1, Cs0, B0, n7486_2_p11, Cs0, B1, n7486_2_p14
  // _7408 7408_1: pin names not known; wires that end beside it: n7404_1_p6, Cs1, n7408_1_p3, Cs2, Cs0, n7408_1_p6, 1'b0, 1'b1, n7404_1_p6, n7404_1_p4, n7404_1_p9, Cs2, n7404_1_p2, n7404_1_p11
  // _7408 7408_2: pin names not known; wires that end beside it: n7408_1_p3, Cs0, n7408_2_p3, n7404_1_p10, n7404_1_p12, n7404_1_p13, 1'b0, 1'b1
  // _74157 74157_1: pin names not known; wires that end beside it: n7408_2_p3, A3, n7486_1_p3, n74157_1_p4, A2, n7486_1_p6, n74157_1_p7, 1'b0, 1'b1, 1'b0, A0, n7486_1_p11, n74157_1_p13, A1, n7486_1_p14, n74157_1_p16
  // _74157 74157_2: pin names not known; wires that end beside it: n7408_1_p6, n7486_2_p3, 1'b1, n74157_2_p4, n7486_2_p6, 1'b1, n74157_2_p7, 1'b1, n74157_2_p9, n7486_2_p11, 1'b1, n74157_2_p12, n7486_2_p14, 1'b1, n74157_2_p15
  // _7483 7483_1: pin names not known; wires that end beside it: 1'b0, 1'b0, 1'b0, 1'b1, C, 1'b0, n7483_1_p7, 1'b0, n74157_2_p4
  // _7483 7483_2: pin names not known; wires that end beside it: 1'b0, 1'b0, 1'b0, S2, n74157_1_p7, n74157_2_p7, 1'b1, S1, n74157_2_p15, n74157_1_p16, n74157_1_p4, S, 1'b0, n7483_1_p7, n7404_1_p14, 1'b0, n74157_2_p12, n74157_1_p13, S0
  // _7432 7432_1: pin names not known; wires that end beside it: n7408_1_p3, n7404_1_p11, n74157_2_p9, n7432_1_p4, n7432_1_p5, n7432_1_p6, 1'b0, 1'b1, S1, S0, n7432_1_p4, S2, S, n7432_1_p5
  // _7486 7486_3: pin names not known; wires that end beside it: C, n7483_1_p7, V, 1'b1, n7432_1_p6, Z, 1'b0, 1'b1

  assign Cout = C;
  assign S3 = S;

  // Notes on the sheet:
  //   Cin
endmodule
