// Logisim project FractionAdder.circ as structural Verilog: 1 circuit, main circuit Adder
module Adder (
  input  [31:0] A,
  input  [31:0] B,
  input  Sa,
  input  Sb,
  output Cout,
  output [31:0] Output_Fraction,
  output Output_Sign
);

  wire comparator_1_eq, comparator_1_gt, multiplexer_1_out, multiplexer_3_out, xor_1_out;
  wire [31:0] adder_1_out, multiplexer_2_out, negator_1_out, subtractor_1_out;

  Comparator #(.width(32), .mode("unsigned")) comparator_1 (
    .a(B), .b(A), .gt(comparator_1_gt), .eq(comparator_1_eq));  // open: lt
  xor xor_1 (xor_1_out, Sa, Sb);
  Adder_part #(.width(32)) adder_1 (.a(A), .b(B), .out(adder_1_out), .cin(1'b0), .cout(Cout));
  Subtractor #(.width(32)) subtractor_1 (.a(A), .b(B), .out(subtractor_1_out));  // open: bin, bout
  Negator #(.width(32)) negator_1 (.in(subtractor_1_out), .out(negator_1_out));
  Multiplexer multiplexer_1 (.in0(Sa), .in1(Sb), .out(multiplexer_1_out), .sel(comparator_1_gt), .en(1'b1));
  Multiplexer #(.width(32)) multiplexer_2 (
    .in0(subtractor_1_out), .in1(negator_1_out), .out(multiplexer_2_out), .sel(comparator_1_gt), .en(1'b1));
  Multiplexer multiplexer_3 (
    .in0(multiplexer_1_out), .in1(1'b0), .out(multiplexer_3_out), .sel(comparator_1_eq), .en(1'b1));
  Multiplexer #(.width(32)) multiplexer_4 (
    .in0(adder_1_out), .in1(multiplexer_2_out), .out(Output_Fraction), .sel(xor_1_out), .en(1'b1));
  Multiplexer multiplexer_5 (.in0(Sa), .in1(multiplexer_3_out), .out(Output_Sign), .sel(xor_1_out), .en(1'b1));
endmodule
