// Logisim project Input.circ as structural Verilog: 3 circuits, main circuit InputSplitter
module InputSplitter (
  input  [31:0] A,
  output [31:0] _32bit_fraction,
  output [8:0] Exponent,
  output Sign_bit
);


  assign _32bit_fraction = {2'b01, A[21:0], {8{1'b0}}};
  assign Exponent = A[30:22];
  assign Sign_bit = A[31];
endmodule

module InputProcessor (
  input  [31:0] A,
  input  [31:0] B,
  output [31:0] Larger_Fraction,
  output [8:0] Larger_Exponent,
  output Larger_Sign,
  output Smaller_Sign,
  output [31:0] Smaller_Fraction,
  output [31:0] Shifted_Smaller_Fraction
);

  wire exponentcomparator_1_ea_eb, exponentcomparator_1_shifterchecker, inputsplitter_1_sign_bit,
       inputsplitter_2_sign_bit;
  wire [4:0] exponentcomparator_1_ea_neb;
  wire [8:0] inputsplitter_1_exponent, inputsplitter_2_exponent;
  wire [31:0] inputsplitter_1__32bit_fraction, inputsplitter_2__32bit_fraction, shifter_1_out;

  InputSplitter inputsplitter_1 (
    .A(A), ._32bit_fraction(inputsplitter_1__32bit_fraction), .Exponent(inputsplitter_1_exponent),
    .Sign_bit(inputsplitter_1_sign_bit));
  InputSplitter inputsplitter_2 (
    .A(B), ._32bit_fraction(inputsplitter_2__32bit_fraction), .Exponent(inputsplitter_2_exponent),
    .Sign_bit(inputsplitter_2_sign_bit));
  ExponentComparator exponentcomparator_1 (
    .Ea(inputsplitter_1_exponent), .Eb(inputsplitter_2_exponent), .Sa(inputsplitter_1_sign_bit),
    .Sb(inputsplitter_2_sign_bit), .Ea_Eb(exponentcomparator_1_ea_eb), .Ea_nEb(exponentcomparator_1_ea_neb),
    .Larger_Exponent(Larger_Exponent), .ShifterChecker(exponentcomparator_1_shifterchecker),
    .Larger_Sign(Larger_Sign), .Smaller_Sign(Smaller_Sign));
  Multiplexer #(.width(32)) multiplexer_1 (
    .in0(inputsplitter_2__32bit_fraction), .in1(inputsplitter_1__32bit_fraction), .out(Larger_Fraction),
    .sel(exponentcomparator_1_ea_eb), .en(1'b1));
  Multiplexer #(.width(32)) multiplexer_2 (
    .in0(inputsplitter_1__32bit_fraction), .in1(inputsplitter_2__32bit_fraction), .out(Smaller_Fraction),
    .sel(exponentcomparator_1_ea_eb), .en(1'b1));
  Shifter #(.width(32), .shift("lr")) shifter_1 (
    .in(Smaller_Fraction), .\dist (exponentcomparator_1_ea_neb), .out(shifter_1_out));
  Multiplexer #(.width(32)) multiplexer_3 (
    .in0(shifter_1_out), .in1({32{1'b0}}), .out(Shifted_Smaller_Fraction),
    .sel(exponentcomparator_1_shifterchecker), .en(1'b1));
endmodule

module ExponentComparator (
  input  [8:0] Ea,
  input  [8:0] Eb,
  input  Sa,
  input  Sb,
  output Ea_Eb,
  output [4:0] Ea_nEb,
  output [8:0] Larger_Exponent,
  output ShifterChecker,
  output Larger_Sign,
  output Smaller_Sign
);

  wire [8:0] multiplexer_2_out;
  wire [9:5] subtractor_1_out;

  Comparator #(.width(9), .mode("unsigned")) comparator_1 (.a(Ea), .b(Eb), .gt(Ea_Eb));  // open: eq, lt
  Multiplexer #(.width(9)) multiplexer_1 (.in0(Eb), .in1(Ea), .out(Larger_Exponent), .sel(Ea_Eb), .en(1'b1));
  Multiplexer #(.width(9)) multiplexer_2 (.in0(Ea), .in1(Eb), .out(multiplexer_2_out), .sel(Ea_Eb), .en(1'b1));
  Multiplexer multiplexer_3 (.in0(Sb), .in1(Sa), .out(Larger_Sign), .sel(Ea_Eb), .en(1'b1));
  Multiplexer multiplexer_4 (.in0(Sa), .in1(Sb), .out(Smaller_Sign), .sel(Ea_Eb), .en(1'b1));
  Subtractor #(.width(10)) subtractor_1 (
    .a({1'b0, Larger_Exponent}), .b({1'b0, multiplexer_2_out}), .out({subtractor_1_out, Ea_nEb}));  // open: bin, bout
  or or_1 (ShifterChecker, subtractor_1_out[5], subtractor_1_out[6], subtractor_1_out[7], subtractor_1_out[8], subtractor_1_out[9]);
endmodule
