// Logisim project Main.circ as structural Verilog: 2 circuits, main circuit main
module main (
  input  [31:0] A,
  input  [31:0] B,
  output Infinity,
  output NaN,
  output [31:0] Output,
  output Overflow,
  output Underflow,
  output Denormalizer
);

  wire adder_1_output_sign, inputprocessor_1_larger_sign, inputprocessor_1_smaller_sign, normalizer_1_msb,
       normalizer_1_overflow, roundednormalizer_1_overflow;
  wire [8:0] inputprocessor_1_larger_exponent, normalizer_1_normalized_exponent,
       roundednormalizer_1_normalized_exp;
  wire [31:0] adder_1_output_fraction, inputprocessor_1_larger_fraction,
       inputprocessor_1_shifted_smaller_fraction, normalizer_1_normalized_fraction,
       roundednormalizer_1_normalized_significand, rounder_1_rounded_significand;

  InputProcessor inputprocessor_1 (
    .A(A), .B(B), .Larger_Fraction(inputprocessor_1_larger_fraction),
    .Larger_Exponent(inputprocessor_1_larger_exponent), .Larger_Sign(inputprocessor_1_larger_sign),
    .Smaller_Sign(inputprocessor_1_smaller_sign),
    .Shifted_Smaller_Fraction(inputprocessor_1_shifted_smaller_fraction));  // open: Smaller_Fraction
  Adder adder_1 (
    .A(inputprocessor_1_larger_fraction), .B(inputprocessor_1_shifted_smaller_fraction),
    .Sa(inputprocessor_1_larger_sign), .Sb(inputprocessor_1_smaller_sign),
    .Output_Fraction(adder_1_output_fraction), .Output_Sign(adder_1_output_sign));  // open: Cout
  Normalizer normalizer_1 (
    .Significand(adder_1_output_fraction), .Exponent_Input(inputprocessor_1_larger_exponent),
    .Normalized_Exponent(normalizer_1_normalized_exponent),
    .Normalized_Fraction(normalizer_1_normalized_fraction), .Overflow(normalizer_1_overflow),
    .MSB(normalizer_1_msb), .Underflow(Underflow), .denormalized(Denormalizer));
  Rounder rounder_1 (
    .significand(normalizer_1_normalized_fraction), .rounded_significand(rounder_1_rounded_significand));
  OutputMarger outputmarger_1 (
    .Fraction(roundednormalizer_1_normalized_significand), .Exponent(roundednormalizer_1_normalized_exp),
    .Sign(adder_1_output_sign), .Output(Output));
  RoundedNormalizer roundednormalizer_1 (
    .Exponent(normalizer_1_normalized_exponent), .Significand(rounder_1_rounded_significand),
    .MSB(normalizer_1_msb), .Overflow(roundednormalizer_1_overflow),
    .Normalized_Exp(roundednormalizer_1_normalized_exp),
    .Normalized_Significand(roundednormalizer_1_normalized_significand), .INFINITY(Infinity), .NaN(NaN));
  or or_1 (Overflow, roundednormalizer_1_overflow, normalizer_1_overflow);
endmodule

module OutputMarger (
  input  [31:0] Fraction,
  input  [8:0] Exponent,
  input  Sign,
  output [31:0] Output
);


  assign Output = {Sign, Exponent, Fraction[29:8]};
endmodule
