// Logisim project Normalizer.circ as structural Verilog: 3 circuits, main circuit Normalizer
module Normalizer (
  input  [8:0] Exponent_Input,
  input  [31:0] Significand,
  output [8:0] Normalized_Exponent,
  output [31:0] Normalized_Fraction,
  output Overflow,
  output MSB,
  output Underflow,
  output denormalized
);

  wire addersubstractor_1_overflow, addersubstractor_1_underflow, and_1_out, comparator_1_eq, not_1_out,
       not_2_out, not_3_out, not_4_out, priority_encoder_1_en_out, zeroonechecker_1_zerochecker;
  wire [4:0] multiplexer_1_out, priority_encoder_1_out, subtractor_1_out;
  wire [8:0] addersubstractor_1_output_exponent;
  wire [31:0] multiplexer_2_out, shifter_1_out, shifter_2_out;

  not not_1 (not_1_out, Significand[31]);
  and and_1 (and_1_out, not_1_out, priority_encoder_1_en_out);
  Priority_Encoder #(.select(5)) priority_encoder_1 (
    .in0(Significand[0]), .in1(Significand[1]), .in2(Significand[2]), .in3(Significand[3]),
    .in4(Significand[4]), .in5(Significand[5]), .in6(Significand[6]), .in7(Significand[7]),
    .in8(Significand[8]), .in9(Significand[9]), .in10(Significand[10]), .in11(Significand[11]),
    .in12(Significand[12]), .in13(Significand[13]), .in14(Significand[14]), .in15(Significand[15]),
    .in16(Significand[16]), .in17(Significand[17]), .in18(Significand[18]), .in19(Significand[19]),
    .in20(Significand[20]), .in21(Significand[21]), .in22(Significand[22]), .in23(Significand[23]),
    .in24(Significand[24]), .in25(Significand[25]), .in26(Significand[26]), .in27(Significand[27]),
    .in28(Significand[28]), .in29(Significand[29]), .in30(Significand[30]), .in31(1'b0),
    .out(priority_encoder_1_out), .en_out(priority_encoder_1_en_out), .en_in(1'b1));  // open: gs
  Comparator #(.width(22)) comparator_1 (.a({22{1'b0}}), .b(Significand[29:8]), .eq(comparator_1_eq));  // open: gt, lt
  not not_2 (not_2_out, comparator_1_eq);
  not not_3 (not_3_out, Significand[31]);
  Subtractor #(.width(5)) subtractor_1 (
    .a(5'b11110), .b(priority_encoder_1_out), .out(subtractor_1_out));  // open: bin, bout
  not not_4 (not_4_out, Significand[30]);
  Multiplexer #(.width(5)) multiplexer_1 (
    .in0(subtractor_1_out), .in1(5'b00001), .out(multiplexer_1_out), .sel(Significand[31]), .en(1'b1));
  Shifter #(.width(32)) shifter_1 (.in(Significand), .\dist (multiplexer_1_out), .out(shifter_1_out));
  Shifter #(.width(32), .shift("lr")) shifter_2 (.in(Significand), .\dist (multiplexer_1_out), .out(shifter_2_out));
  and and_2 (denormalized, zeroonechecker_1_zerochecker, not_2_out, not_4_out, not_3_out);
  ZeroOneChecker zeroonechecker_1 (
    .Exponent(Normalized_Exponent), .ZeroChecker(zeroonechecker_1_zerochecker));  // open: OneChecker
  Multiplexer #(.width(32)) multiplexer_2 (
    .in0(shifter_1_out), .in1(shifter_2_out), .out(multiplexer_2_out), .sel(Significand[31]), .en(1'b1));
  AdderSubstractor addersubstractor_1 (
    .Input_Exp(Exponent_Input), .Amount(multiplexer_1_out), .add_sub(Significand[31]),
    .overflow(addersubstractor_1_overflow), .output_exponent(addersubstractor_1_output_exponent),
    .underflow(addersubstractor_1_underflow));
  Multiplexer #(.width(9)) multiplexer_3 (
    .in0(addersubstractor_1_output_exponent), .in1({9{1'b0}}), .out(Normalized_Exponent), .sel(and_1_out),
    .en(1'b1));
  Multiplexer #(.width(32)) multiplexer_4 (
    .in0(multiplexer_2_out), .in1({32{1'b0}}), .out(Normalized_Fraction), .sel(and_1_out), .en(1'b1));
  Multiplexer multiplexer_5 (.in0(addersubstractor_1_overflow), .in1(1'b0), .out(Overflow), .sel(and_1_out), .en(1'b1));
  Multiplexer multiplexer_6 (
    .in0(addersubstractor_1_underflow), .in1(1'b0), .out(Underflow), .sel(and_1_out), .en(1'b1));

  assign MSB = Significand[31];
endmodule

module ZeroOneChecker (
  input  [8:0] Exponent,
  output ZeroChecker,
  output OneChecker
);

  and and_1 (OneChecker, Exponent[0], Exponent[1], Exponent[2], Exponent[3], Exponent[4], Exponent[5], Exponent[6], Exponent[7], Exponent[8]);
  nor nor_1 (ZeroChecker, Exponent[0], Exponent[1], Exponent[2], Exponent[3], Exponent[4], Exponent[5], Exponent[6], Exponent[7], Exponent[8]);
endmodule

module AdderSubstractor (
  input  [8:0] Input_Exp,
  input  [4:0] Amount,
  input  add_sub,
  output overflow,
  output [8:0] output_exponent,
  output underflow
);

  wire adder_1_cout, not_1_out, or_1_out, or_2_out, subtractor_1_bout, zeroonechecker_1_onechecker,
       zeroonechecker_1_zerochecker;
  wire [8:0] adder_1_out, subtractor_1_out;

  Subtractor #(.width(9)) subtractor_1 (
    .a(Input_Exp), .b({4'b0000, Amount}), .out(subtractor_1_out), .bin(1'b0), .bout(subtractor_1_bout));
  Adder #(.width(9)) adder_1 (.a(Input_Exp), .b({4'b0000, Amount}), .out(adder_1_out), .cin(1'b0), .cout(adder_1_cout));
  ZeroOneChecker zeroonechecker_1 (
    .Exponent(output_exponent), .ZeroChecker(zeroonechecker_1_zerochecker),
    .OneChecker(zeroonechecker_1_onechecker));
  or or_1 (or_1_out, subtractor_1_bout, zeroonechecker_1_zerochecker);
  not not_1 (not_1_out, add_sub);
  and and_1 (underflow, not_1_out, or_1_out);
  or or_2 (or_2_out, zeroonechecker_1_onechecker, adder_1_cout);
  Multiplexer #(.width(9), .disabled(0), .enable("false")) multiplexer_1 (
    .in0(subtractor_1_out), .in1(adder_1_out), .out(output_exponent), .sel(add_sub));
  and and_2 (overflow, or_2_out, add_sub);
endmodule
