// Logisim project RoundedNormalizer.circ as structural Verilog: 1 circuit, main circuit RoundedNormalizer
module RoundedNormalizer (
  input  [8:0] Exponent,
  input  [31:0] Significand,
  input  MSB,
  output Overflow,
  output [8:0] Normalized_Exp,
  output [31:0] Normalized_Significand,
  output INFINITY,
  output NaN
);

  wire adder_1_cout, comparator_1_eq, not_1_out, or_1_out, zeroonechecker_1_onechecker,
       zeroonechecker_1_zerochecker;
  wire [31:0] shifter_1_out;

  Adder #(.width(9)) adder_1 (
    .a(Exponent), .b({9{1'b0}}), .out(Normalized_Exp), .cin(Significand[31]), .cout(adder_1_cout));
  Shifter #(.width(32), .shift("lr")) shifter_1 (.in(Significand), .\dist (5'b00001), .out(shifter_1_out));
  Multiplexer #(.width(32), .disabled(0), .enable("false")) multiplexer_1 (
    .in0(Significand), .in1(shifter_1_out), .out(Normalized_Significand), .sel(Significand[31]));
  Comparator #(.width(22)) comparator_1 (
    .a(Normalized_Significand[29:8]), .b({22{1'b0}}), .eq(comparator_1_eq));  // open: gt, lt
  ZeroOneChecker zeroonechecker_1 (
    .Exponent(Normalized_Exp), .ZeroChecker(zeroonechecker_1_zerochecker),
    .OneChecker(zeroonechecker_1_onechecker));
  or or_1 (or_1_out, zeroonechecker_1_zerochecker, adder_1_cout);
  not not_1 (not_1_out, comparator_1_eq);
  and and_1 (Overflow, or_1_out, Significand[31]);
  and and_2 (INFINITY, zeroonechecker_1_onechecker, MSB, comparator_1_eq);
  and and_3 (NaN, not_1_out, MSB, zeroonechecker_1_onechecker);
endmodule
