// Logisim project Rounder.circ as structural Verilog: 1 circuit, main circuit Rounder
module Rounder (
  input  [31:0] significand,
  output [31:0] rounded_significand
);

  wire and_1_out, and_2_out, or_1_out, or_2_out, or_3_out;

  or or_1 (or_1_out, significand[0], significand[1], significand[2], significand[3], significand[4], significand[5]);
  or or_2 (or_2_out, or_1_out, significand[6]);
  and and_1 (and_1_out, or_2_out, significand[7]);
  and and_2 (and_2_out, significand[8], significand[7]);
  or or_3 (or_3_out, and_1_out, and_2_out);
  Adder #(.width(24)) adder_1 (
    .a(significand[31:8]), .b({24{1'b0}}), .out(rounded_significand[31:8]), .cin(or_3_out));  // open: cout

  assign rounded_significand[7:0] = {8{1'b0}};
endmodule
